# Fritzing sketch bbox2025_fritzing (saved by Fritzing 1.0.5)

parts:
  SCORPIO = Adafruit Feather RP2040 SCORPIO [part_number=#5650]
  RPi5 = Raspberry Pi 5  # not connected
  Row_1_/_Face_1_2_3 = Neopixel Strip -- White (60/m)
  Row_2_/_Face_1_2_3 = Neopixel Strip -- White (60/m)
  Row_3_Face_1_2_3 = Neopixel Strip -- White (60/m)
  Row_0_/_Face_1_2_3 = Neopixel Strip -- White (60/m)
  Row_0_Face_0 = Neopixel Strip -- White (60/m)
  Row_1_Face_0 = Neopixel Strip -- White (60/m)
  Row_2_Face_0 = Neopixel Strip -- White (60/m)
  Row_3_Face_0 = Neopixel Strip -- White (60/m)
  JACK1 = 2.1mm Barrel Jack with Terminal Block
  C1 = Capacitor Polarized [package=panasonic_d]
  C2 = Capacitor Polarized [package=panasonic_d]
  C3 = Capacitor Polarized [package=panasonic_d]
  C4 = Capacitor Polarized [package=panasonic_d]
  C5 = Capacitor Polarized [package=panasonic_d]
  C6 = Capacitor Polarized [package=panasonic_d]
  C7 = Capacitor Polarized [package=panasonic_d]
  C8 = Capacitor Polarized [package=panasonic_d]
  J11 = Wago 221-413
  J12 = Wago 221-415
  J13 = Wago 221-415
  J10 = Wago 221-415
  J14 = Wago 221-415
  J15 = Wago 221-415
  J16 = macropaw_beatboxer_small  # not connected

nets:
  GND: SCORPIO.GND, Row_1_/_Face_1_2_3.GND, Row_2_/_Face_1_2_3.GND, Row_3_Face_1_2_3.GND, Row_0_/_Face_1_2_3.GND, Row_0_Face_0.GND, Row_1_Face_0.GND, Row_2_Face_0.GND, Row_3_Face_0.GND, JACK1.NEG, C1.-, C2.-, C3.-, C4.-, C5.-, C6.-, C7.-, C8.-, J12.Pin_1, J12.Pin_2, J12.Pin_3, J12.Pin_5, J13.Pin_1, J13.Pin_2, J13.Pin_3, J13.Pin_4, J13.Pin_5, J15.Pin_1, J15.Pin_2, J15.Pin_3, J15.Pin_4, J15.Pin_5
  N1: SCORPIO.NEO7, Row_3_Face_0.DI
  N2: SCORPIO.NEO6, Row_2_Face_0.DI
  N3: SCORPIO.NEO5, Row_1_Face_0.DI
  N4: SCORPIO.NEO4, Row_0_Face_0.DI
  N5: SCORPIO.NEO3, Row_3_Face_1_2_3.DI
  N6: SCORPIO.NEO2, Row_2_/_Face_1_2_3.DI
  N7: SCORPIO.NEO1, Row_1_/_Face_1_2_3.DI
  N8: SCORPIO.NEO0, Row_0_/_Face_1_2_3.DI
  +5V: Row_1_/_Face_1_2_3.+5V, Row_2_/_Face_1_2_3.+5V, Row_3_Face_1_2_3.+5V, Row_0_/_Face_1_2_3.+5V, Row_0_Face_0.+5V, Row_1_Face_0.+5V, Row_2_Face_0.+5V, Row_3_Face_0.+5V, JACK1.POS, C1.+, C2.+, C3.+, C4.+, C5.+, C6.+, C7.+, C8.+, J11.Pin_1, J11.Pin_2, J11.Pin_3, J10.Pin_1, J10.Pin_2, J10.Pin_3, J10.Pin_4, J10.Pin_5, J14.Pin_1, J14.Pin_2, J14.Pin_3, J14.Pin_4, J14.Pin_5

notes:
  USB-A -> USB-C
  USB-A -> USB-C
  RPi5 -> SCORPIO
  5V 10A switching power supply
  USB-A -> USB-C
  RPi5 -> MacroPaw

custom parts:
  Adafruit Feather RP2040 SCORPIO: If there is one thing Adafruit is known for, its mega-blinky-fun-rainbow-LEDs. We just love sticking NeoPixels anywhere and everywhere. When we saw the new 'PIO' peripheral on the RP2040 from Raspberry Pi, we just knew it would be perfect for driving large quantities of NeoPixels. So we created this board, the Adafruit Feather RP2040 SCORPIO, designed specifically for NeoPixel (WS2812) driving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
  Raspberry Pi 5: The RPi5, a faster version of the awesome Raspberry Pi4B ARM Board with 40 pin gpio.
  Neopixel Strip -- White (60/m): Neopixel Strip, White, 60 pixels per meter.
  Wago 221-413: Wago 221-413 3 position splicing connector 12AWG.
  Wago 221-415: Wago 221-415 5 position splicing connector 12AWG.
  macropaw_beatboxer_small: https://github.com/kodachi614/macropaw/blob/main/Beatboxer
